// Logisim project cpu.circ as structural Verilog: 1 circuit, main circuit main
module main (
);

  wire and_1_out, and_2_out, and_3_out, and_4_out, and_5_out, and_6_out, and_7_out, and_8_out, and_9_out,
       and_10_out, and_11_out, and_12_out, and_13_out, and_14_out, and_15_out, and_16_out, and_17_out,
       and_18_out, and_19_out, and_20_out, and_21_out, and_22_out, and_23_out, and_24_out, and_25_out,
       and_26_out, button_1_out, button_2_out, button_3_out, clock_1_out, decoder_1_out0, decoder_1_out1,
       decoder_1_out2, decoder_1_out3, decoder_2_out0, decoder_2_out1, decoder_2_out2, decoder_2_out3,
       nor_1_out, not_1_out, not_2_out, or_1_out, or_2_out, or_3_out, or_4_out, or_5_out, or_6_out, or_7_out,
       register_3_q, register_4_q, xor_1_out, xor_2_out, xor_3_out, xor_4_out, xor_5_out, xor_14_out,
       xor_15_out, xor_16_out, xor_17_out, xor_18_out, xor_19_out, xor_20_out, xor_21_out, xor_22_out,
       xor_23_out, xor_24_out, xor_25_out, xor_26_out, xor_27_out, xor_28_out, xor_29_out;
  wire [2:0] multiplexer_2_out, register_2_q, xor_11_out;
  wire [4:0] multiplexer_1_out, register_1_q, rom_1_data, xor_6_out;
  wire [7:0] controlled_buffer_1_out, register_5_q, register_6_q, register_7_q, register_8_q, register_9_q,
       xor_30_out;
  wire [7:5] rom_1_data_2;
  wire [15:0] rom_2_data;

  Clock clock_1 (.out(clock_1_out));
  Button button_1 (.out(button_1_out));
  Button button_2 (.out(button_2_out));
  and and_1 (and_1_out, register_3_q, clock_1_out);
  not not_1 (not_1_out, rom_2_data[7]);
  Multiplexer #(.width(5)) multiplexer_1 (
    .in0(register_1_q), .in1(rom_1_data), .out(multiplexer_1_out), .sel(rom_2_data[7]));
  and and_2 (and_2_out, not_1_out, multiplexer_1_out[0]);
  and and_3 (and_3_out, and_2_out, multiplexer_1_out[1]);
  and and_4 (and_4_out, and_3_out, multiplexer_1_out[2]);
  and and_5 (and_5_out, and_4_out, multiplexer_1_out[3]);
  and and_6 (and_6_out, register_4_q, rom_2_data[6]);
  xor xor_1 (xor_1_out, not_1_out, multiplexer_1_out[0]);
  xor xor_2 (xor_2_out, and_2_out, multiplexer_1_out[1]);
  xor xor_3 (xor_3_out, and_3_out, multiplexer_1_out[2]);
  xor xor_4 (xor_4_out, and_4_out, multiplexer_1_out[3]);
  xor xor_5 (xor_5_out, and_5_out, multiplexer_1_out[4]);
  xor xor_6 (xor_6_out[0], and_6_out, xor_1_out);
  and and_7 (and_7_out, and_6_out, xor_1_out);
  xor xor_7 (xor_6_out[1], and_7_out, xor_2_out);
  and and_8 (and_8_out, and_7_out, xor_2_out);
  xor xor_8 (xor_6_out[2], and_8_out, xor_3_out);
  and and_9 (and_9_out, and_8_out, xor_3_out);
  xor xor_9 (xor_6_out[3], and_9_out, xor_4_out);
  and and_10 (and_10_out, and_9_out, xor_4_out);
  xor xor_10 (xor_6_out[4], and_10_out, xor_5_out);
  Register #(.width(5)) register_1 (
    .D(xor_6_out), .en(rom_2_data[15]), .clk(and_1_out), .Q(register_1_q), .clr(button_1_out));
  ROM #(.addrWidth(5)) rom_1 (.addr(register_1_q), .data({rom_1_data_2, rom_1_data}));
  Multiplexer #(.width(3)) multiplexer_2 (
    .in0(register_2_q), .in1(3'b111), .out(multiplexer_2_out), .sel(rom_2_data[15]));
  xor xor_11 (xor_11_out[0], 1'b1, multiplexer_2_out[0]);
  and and_11 (and_11_out, 1'b1, multiplexer_2_out[0]);
  xor xor_12 (xor_11_out[1], and_11_out, multiplexer_2_out[1]);
  and and_12 (and_12_out, multiplexer_2_out[1], and_11_out);
  xor xor_13 (xor_11_out[2], and_12_out, multiplexer_2_out[2]);
  Register #(.width(3)) register_2 (.D(xor_11_out), .en(1'b1), .clk(and_1_out), .Q(register_2_q), .clr(button_1_out));
  ROM #(.addrWidth(6), .dataWidth(16)) rom_2 (.addr({rom_1_data_2, register_2_q}), .data(rom_2_data));
  not not_2 (not_2_out, register_3_q);
  Register #(.width(1)) register_3 (
    .D(not_2_out), .en(button_2_out), .clk(button_2_out), .Q(register_3_q), .clr(rom_2_data[8]));
  nor nor_1 (nor_1_out, controlled_buffer_1_out[7], controlled_buffer_1_out[6], controlled_buffer_1_out[5], controlled_buffer_1_out[4], controlled_buffer_1_out[3], controlled_buffer_1_out[2], controlled_buffer_1_out[1], controlled_buffer_1_out[0]);
  Register #(.width(1)) register_4 (
    .D(nor_1_out), .en(rom_2_data[5]), .clk(and_1_out), .Q(register_4_q), .clr(button_1_out));
  Decoder #(.select(2)) decoder_1 (
    .out0(decoder_1_out0), .out1(decoder_1_out1), .out2(decoder_1_out2), .out3(decoder_1_out3),
    .sel(rom_1_data[1:0]), .en(rom_2_data[3]));
  Register register_5 (
    .D(controlled_buffer_1_out), .en(decoder_1_out3), .clk(and_1_out), .Q(register_5_q), .clr(button_1_out));
  Register register_6 (
    .D(controlled_buffer_1_out), .en(decoder_1_out2), .clk(and_1_out), .Q(register_6_q), .clr(button_1_out));
  Register register_7 (
    .D(controlled_buffer_1_out), .en(decoder_1_out1), .clk(and_1_out), .Q(register_7_q), .clr(button_1_out));
  Register register_8 (
    .D(controlled_buffer_1_out), .en(decoder_1_out0), .clk(and_1_out), .Q(register_8_q), .clr(button_1_out));
  Decoder #(.select(2)) decoder_2 (
    .out0(decoder_2_out0), .out1(decoder_2_out1), .out2(decoder_2_out2), .out3(decoder_2_out3),
    .sel(rom_1_data[1:0]), .en(rom_2_data[2]));
  assign controlled_buffer_1_out[0] = decoder_2_out3 ? register_5_q[0] : 1'bz;  // Controlled_Buffer controlled_buffer_1
  assign controlled_buffer_1_out[1] = decoder_2_out3 ? register_5_q[1] : 1'bz;  // Controlled_Buffer controlled_buffer_2
  assign controlled_buffer_1_out[2] = decoder_2_out3 ? register_5_q[2] : 1'bz;  // Controlled_Buffer controlled_buffer_3
  assign controlled_buffer_1_out[3] = decoder_2_out3 ? register_5_q[3] : 1'bz;  // Controlled_Buffer controlled_buffer_4
  assign controlled_buffer_1_out[4] = decoder_2_out3 ? register_5_q[4] : 1'bz;  // Controlled_Buffer controlled_buffer_5
  assign controlled_buffer_1_out[5] = decoder_2_out3 ? register_5_q[5] : 1'bz;  // Controlled_Buffer controlled_buffer_6
  assign controlled_buffer_1_out[6] = decoder_2_out3 ? register_5_q[6] : 1'bz;  // Controlled_Buffer controlled_buffer_7
  assign controlled_buffer_1_out[7] = decoder_2_out3 ? register_5_q[7] : 1'bz;  // Controlled_Buffer controlled_buffer_8
  assign controlled_buffer_1_out[0] = decoder_2_out2 ? register_6_q[0] : 1'bz;  // Controlled_Buffer controlled_buffer_9
  assign controlled_buffer_1_out[1] = decoder_2_out2 ? register_6_q[1] : 1'bz;  // Controlled_Buffer controlled_buffer_10
  assign controlled_buffer_1_out[2] = decoder_2_out2 ? register_6_q[2] : 1'bz;  // Controlled_Buffer controlled_buffer_11
  assign controlled_buffer_1_out[3] = decoder_2_out2 ? register_6_q[3] : 1'bz;  // Controlled_Buffer controlled_buffer_12
  assign controlled_buffer_1_out[4] = decoder_2_out2 ? register_6_q[4] : 1'bz;  // Controlled_Buffer controlled_buffer_13
  assign controlled_buffer_1_out[5] = decoder_2_out2 ? register_6_q[5] : 1'bz;  // Controlled_Buffer controlled_buffer_14
  assign controlled_buffer_1_out[6] = decoder_2_out2 ? register_6_q[6] : 1'bz;  // Controlled_Buffer controlled_buffer_15
  assign controlled_buffer_1_out[7] = decoder_2_out2 ? register_6_q[7] : 1'bz;  // Controlled_Buffer controlled_buffer_16
  assign controlled_buffer_1_out[0] = decoder_2_out1 ? register_7_q[0] : 1'bz;  // Controlled_Buffer controlled_buffer_17
  assign controlled_buffer_1_out[1] = decoder_2_out1 ? register_7_q[1] : 1'bz;  // Controlled_Buffer controlled_buffer_18
  assign controlled_buffer_1_out[2] = decoder_2_out1 ? register_7_q[2] : 1'bz;  // Controlled_Buffer controlled_buffer_19
  assign controlled_buffer_1_out[3] = decoder_2_out1 ? register_7_q[3] : 1'bz;  // Controlled_Buffer controlled_buffer_20
  assign controlled_buffer_1_out[4] = decoder_2_out1 ? register_7_q[4] : 1'bz;  // Controlled_Buffer controlled_buffer_21
  assign controlled_buffer_1_out[5] = decoder_2_out1 ? register_7_q[5] : 1'bz;  // Controlled_Buffer controlled_buffer_22
  assign controlled_buffer_1_out[6] = decoder_2_out1 ? register_7_q[6] : 1'bz;  // Controlled_Buffer controlled_buffer_23
  assign controlled_buffer_1_out[7] = decoder_2_out1 ? register_7_q[7] : 1'bz;  // Controlled_Buffer controlled_buffer_24
  assign controlled_buffer_1_out[0] = decoder_2_out0 ? register_8_q[0] : 1'bz;  // Controlled_Buffer controlled_buffer_25
  assign controlled_buffer_1_out[1] = decoder_2_out0 ? register_8_q[1] : 1'bz;  // Controlled_Buffer controlled_buffer_26
  assign controlled_buffer_1_out[2] = decoder_2_out0 ? register_8_q[2] : 1'bz;  // Controlled_Buffer controlled_buffer_27
  assign controlled_buffer_1_out[3] = decoder_2_out0 ? register_8_q[3] : 1'bz;  // Controlled_Buffer controlled_buffer_28
  assign controlled_buffer_1_out[4] = decoder_2_out0 ? register_8_q[4] : 1'bz;  // Controlled_Buffer controlled_buffer_29
  assign controlled_buffer_1_out[5] = decoder_2_out0 ? register_8_q[5] : 1'bz;  // Controlled_Buffer controlled_buffer_30
  assign controlled_buffer_1_out[6] = decoder_2_out0 ? register_8_q[6] : 1'bz;  // Controlled_Buffer controlled_buffer_31
  assign controlled_buffer_1_out[7] = decoder_2_out0 ? register_8_q[7] : 1'bz;  // Controlled_Buffer controlled_buffer_32
  xor xor_14 (xor_14_out, rom_2_data[4], 1'b0);
  xor xor_15 (xor_15_out, rom_2_data[4], 1'b0);
  xor xor_16 (xor_16_out, rom_2_data[4], 1'b0);
  xor xor_17 (xor_17_out, rom_2_data[4], 1'b0);
  xor xor_18 (xor_18_out, rom_2_data[4], 1'b0);
  xor xor_19 (xor_19_out, rom_2_data[4], 1'b0);
  xor xor_20 (xor_20_out, rom_2_data[4], 1'b0);
  xor xor_21 (xor_21_out, rom_2_data[4], 1'b1);
  xor xor_22 (xor_22_out, controlled_buffer_1_out[0], xor_21_out);
  xor xor_23 (xor_23_out, controlled_buffer_1_out[1], xor_14_out);
  xor xor_24 (xor_24_out, controlled_buffer_1_out[2], xor_15_out);
  xor xor_25 (xor_25_out, controlled_buffer_1_out[3], xor_16_out);
  xor xor_26 (xor_26_out, controlled_buffer_1_out[4], xor_17_out);
  xor xor_27 (xor_27_out, controlled_buffer_1_out[5], xor_18_out);
  xor xor_28 (xor_28_out, controlled_buffer_1_out[6], xor_19_out);
  xor xor_29 (xor_29_out, controlled_buffer_1_out[7], xor_20_out);
  xor xor_30 (xor_30_out[0], xor_22_out, rom_2_data[4]);
  and and_13 (and_13_out, xor_22_out, rom_2_data[4]);
  and and_14 (and_14_out, controlled_buffer_1_out[0], xor_21_out);
  xor xor_31 (xor_30_out[1], xor_23_out, or_1_out);
  and and_15 (and_15_out, xor_23_out, or_1_out);
  and and_16 (and_16_out, controlled_buffer_1_out[1], xor_14_out);
  xor xor_32 (xor_30_out[2], xor_24_out, or_2_out);
  and and_17 (and_17_out, xor_24_out, or_2_out);
  and and_18 (and_18_out, controlled_buffer_1_out[2], xor_15_out);
  xor xor_33 (xor_30_out[3], xor_25_out, or_3_out);
  and and_19 (and_19_out, xor_25_out, or_3_out);
  and and_20 (and_20_out, controlled_buffer_1_out[3], xor_16_out);
  xor xor_34 (xor_30_out[4], xor_26_out, or_4_out);
  and and_21 (and_21_out, xor_26_out, or_4_out);
  and and_22 (and_22_out, controlled_buffer_1_out[4], xor_17_out);
  xor xor_35 (xor_30_out[5], xor_27_out, or_5_out);
  and and_23 (and_23_out, xor_27_out, or_5_out);
  and and_24 (and_24_out, controlled_buffer_1_out[5], xor_18_out);
  xor xor_36 (xor_30_out[6], xor_28_out, or_6_out);
  and and_25 (and_25_out, xor_28_out, or_6_out);
  and and_26 (and_26_out, controlled_buffer_1_out[6], xor_19_out);
  xor xor_37 (xor_30_out[7], xor_29_out, or_7_out);
  or or_1 (or_1_out, and_13_out, and_14_out);
  or or_2 (or_2_out, and_15_out, and_16_out);
  or or_3 (or_3_out, and_17_out, and_18_out);
  or or_4 (or_4_out, and_19_out, and_20_out);
  or or_5 (or_5_out, and_21_out, and_22_out);
  or or_6 (or_6_out, and_23_out, and_24_out);
  or or_7 (or_7_out, and_25_out, and_26_out);
  Register register_9 (.D(xor_30_out), .en(rom_2_data[1]), .clk(and_1_out), .Q(register_9_q), .clr(button_3_out));
  Button button_3 (.out(button_3_out));
  assign controlled_buffer_1_out[0] = rom_2_data[0] ? register_9_q[0] : 1'bz;  // Controlled_Buffer controlled_buffer_33
  assign controlled_buffer_1_out[1] = rom_2_data[0] ? register_9_q[1] : 1'bz;  // Controlled_Buffer controlled_buffer_34
  assign controlled_buffer_1_out[2] = rom_2_data[0] ? register_9_q[2] : 1'bz;  // Controlled_Buffer controlled_buffer_35
  assign controlled_buffer_1_out[3] = rom_2_data[0] ? register_9_q[3] : 1'bz;  // Controlled_Buffer controlled_buffer_36
  assign controlled_buffer_1_out[4] = rom_2_data[0] ? register_9_q[4] : 1'bz;  // Controlled_Buffer controlled_buffer_37
  assign controlled_buffer_1_out[5] = rom_2_data[0] ? register_9_q[5] : 1'bz;  // Controlled_Buffer controlled_buffer_38
  assign controlled_buffer_1_out[6] = rom_2_data[0] ? register_9_q[6] : 1'bz;  // Controlled_Buffer controlled_buffer_39
  assign controlled_buffer_1_out[7] = rom_2_data[0] ? register_9_q[7] : 1'bz;  // Controlled_Buffer controlled_buffer_40
  Pull_Resistor pull_resistor_1 (.node(controlled_buffer_1_out[7]));
  Pull_Resistor pull_resistor_2 (.node(controlled_buffer_1_out[6]));
  Pull_Resistor pull_resistor_3 (.node(controlled_buffer_1_out[5]));
  Pull_Resistor pull_resistor_4 (.node(controlled_buffer_1_out[4]));
  Pull_Resistor pull_resistor_5 (.node(controlled_buffer_1_out[3]));
  Pull_Resistor pull_resistor_6 (.node(controlled_buffer_1_out[2]));
  Pull_Resistor pull_resistor_7 (.node(controlled_buffer_1_out[1]));
  Pull_Resistor pull_resistor_8 (.node(controlled_buffer_1_out[0]));

  // Notes on the sheet:
  //   reset
  //   run
  //   contents of rom_1 (hex, n*v repeats v):
  //   81 63 e0 20 41 60
  //   Address
  //   contents of rom_2 (hex, n*v repeats v):
  //   8*0 6 9 8000 5*0 16 19 8000 5*0 8080 7*0 24 8040 22*0 100
endmodule
